# Fritzing sketch Huzzah_Shirt (saved by Fritzing 0.9.3b)

parts:
  Part1 = Adafruit Feather HUZZAH ESP8266 [part_number="Adafruit #2821"]
  U1 = LIPO-2000mAh [package=lipo-2000]  # not connected
  Part2 = Adafruit Switched JST Breakout [part_number="Adafruit #1863"]
  NEOPIXEL2 = Neopixel Strip -- Black (60/m)
  NEOPIXEL3 = Neopixel Strip -- Black (60/m)
  NEOPIXEL4 = Neopixel Strip -- Black (60/m)

nets:
  GND: Part1.GND, Part2.GND, NEOPIXEL2.GND, NEOPIXEL3.GND, NEOPIXEL4.GND
  +5V: Part1.VBAT, Part2.SW, NEOPIXEL2.+5V, NEOPIXEL3.+5V, NEOPIXEL4.+5V
  N1: Part1.GPIO2, NEOPIXEL2.DI
  N2: Part1.GPIO5/SCL, NEOPIXEL3.DI
  N3: Part1.GPIO4/SDA, NEOPIXEL4.DI

custom parts:
  Adafruit Feather HUZZAH ESP8266: his is the Adafruit Feather HUZZAH ESP8266 - our take on an 'all-in-one' ESP8266 WiFi development board with built in USB and battery charging. Its an ESP8266 WiFi module with all the extras you need, ready to rock! We have other boards in the Feather family, check'em out here. At the Feather HUZZAH's heart is an ESP8266 WiFi microcontroller clocked at 80 MHz and at 3.3V logic. This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
  Adafruit Switched JST Breakout: This switched JST connector is the best way to quickly prototype with our LiPoly batteries. We paired a genuine JST connector with a slide switch that can do up to 600mA. Both are soldered onto a breadboard-friendly breakout. There's two ground pins, one 'switched' power pin, and one pin that is always on. This is compatible with the "JST PH 2-pin" connectors we use in our battery packs..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
  Neopixel Strip -- Black (60/m): Neopixel Strip, Black, 60 pixels per meter.
